// Logisim project baseball_circuit.circ as structural Verilog: 10 circuits, main circuit main
module main (
  input  [3:0] first_hitter,
  input  [3:0] first_batter,
  input  [3:0] second_hitter,
  input  [3:0] second_batter,
  input  [3:0] third_hitter,
  input  [3:0] third_batter,
  input  [3:0] fourth_hitter,
  input  [3:0] fourth_batter,
  input  [3:0] fifth_hitter,
  input  [3:0] fifth_batter,
  input  [3:0] sixth_hitter,
  input  [3:0] sixth_batter,
  input  [3:0] seventh_hitter,
  input  [3:0] seventh_batter,
  input  [3:0] eighth_hitter,
  input  [3:0] eighth_batter,
  input  [3:0] nineth_hitter,
  input  [3:0] nineth_batter,
  input  En_signal,
  input  Enable_signal
);

  wire and_1_out, comparator_1_eq, comparator_2_eq, first_base, first_runner, rgbled_4_p1, second_base,
       second_runner, third_base, third_runner, TOP_BOTTOM;
  wire [1:0] Outs, Outs_home;
  wire [3:0] INNING, THE_CURRENT_BATTER, THE_CURRENT_HITTER, total_awayH, total_awayL, total_homeH,
       total_homeL;
  wire [3:3] baseball_1_runner_position, baseball_2_runner_position;
  wire [4:0] H_signal, H_signal_home;

  // RGBLED rgbled_1: pin names not known; wires that end beside it: third_base
  LED led_1 (.in(Outs[0]));
  LED single (.in(H_signal[0]));
  LED double (.in(H_signal[1]));
  LED triple (.in(H_signal[2]));
  LED homerun (.in(H_signal[3]));
  LED out_a (.in(H_signal[4]));
  BASEBALL baseball_1 (
    .first(first_hitter), .second(second_hitter), .third(third_hitter), .fourth(fourth_hitter),
    .fifth(fifth_hitter), .sixth(sixth_hitter), .seventh(seventh_hitter), .eighth(eighth_hitter),
    .nineth(nineth_hitter), .in_10(En_signal), .H_signal(H_signal), .total_awayL(total_awayL),
    .total_awayH(total_awayH),
    .runner_position({baseball_1_runner_position[3], third_base, second_base, first_base}), .outs(Outs),
    .the_current(THE_CURRENT_HITTER));  // open: inning
  // RGBLED rgbled_2: pin names not known; wires that end beside it: second_base
  // RGBLED rgbled_3: pin names not known; wires that end beside it: first_base
  LED led_2 (.in(Outs[1]));
  Hex_Digit_Display hex_digit_display_1 (.value(THE_CURRENT_HITTER));  // open: dp
  Hex_Digit_Display hex_digit_display_2 (.value(total_awayH));  // open: dp
  // RGBLED rgbled_4: pin names not known; wires that end beside it: rgbled_4_p1
  not not_1 (rgbled_4_p1, TOP_BOTTOM);
  // RGBLED rgbled_5: pin names not known; wires that end beside it: TOP_BOTTOM
  Hex_Digit_Display hex_digit_display_3 (.value(INNING));  // open: dp
  Hex_Digit_Display hex_digit_display_4 (.value(total_homeH));  // open: dp
  Comparator #(.width(2)) comparator_1 (.a(2'b00), .b(Outs), .eq(comparator_1_eq));  // open: gt, lt
  Comparator #(.width(2)) comparator_2 (.a(Outs_home), .b(2'b00), .eq(comparator_2_eq));  // open: gt, lt
  Hex_Digit_Display hex_digit_display_5 (.value(total_awayL));  // open: dp
  Hex_Digit_Display hex_digit_display_6 (.value(total_homeL));  // open: dp
  and and_1 (and_1_out, comparator_1_eq, comparator_2_eq);
  // RGBLED rgbled_6: pin names not known; wires that end beside it: second_runner
  // RGBLED rgbled_7: pin names not known; wires that end beside it: third_runner
  LED led_3 (.in(Outs_home[0]));
  LED led_4 (.in(Outs_home[1]));
  LED a_single (.in(H_signal_home[0]));
  LED doubles (.in(H_signal_home[1]));
  LED triples (.in(H_signal_home[2]));
  LED a_homerun (.in(H_signal_home[3]));
  LED out_h (.in(H_signal_home[4]));
  T_Flip_Flop t_ff_1 (.T(and_1_out), .clk(and_1_out), .Q(TOP_BOTTOM));  // open: Qn, reset, preset
  // RGBLED rgbled_8: pin names not known; wires that end beside it: first_runner
  Hex_Digit_Display hex_digit_display_7 (.value(THE_CURRENT_BATTER));  // open: dp
  BASEBALL baseball_2 (
    .first(first_batter), .second(second_batter), .third(third_batter), .fourth(fourth_batter),
    .fifth(fifth_batter), .sixth(sixth_batter), .seventh(seventh_batter), .eighth(eighth_batter),
    .nineth(nineth_batter), .in_10(Enable_signal), .H_signal(H_signal_home), .total_awayL(total_homeL),
    .total_awayH(total_homeH),
    .runner_position({baseball_2_runner_position[3], third_runner, second_runner, first_runner}),
    .outs(Outs_home), .the_current(THE_CURRENT_BATTER), .inning(INNING));

  // Other names for the same wires on the sheet: Eighth[3:0] = eighth_hitter; Eighth_man[3:0] = eighth_batter;
  //   Fifth[3:0] = fifth_hitter; Fifth_man[3:0] = fifth_batter; First[3:0] = first_hitter;
  //   First_man[3:0] = first_batter; Fourth[3:0] = fourth_hitter; Fourth_man[3:0] = fourth_batter;
  //   Nineth[3:0] = nineth_hitter; Nineth_man[3:0] = nineth_batter; Second[3:0] = second_hitter;
  //   Second_man[3:0] = second_batter; Seventh[3:0] = seventh_hitter; Seventh_man[3:0] = seventh_batter;
  //   Sixth[3:0] = sixth_hitter; Sixth_man[3:0] = sixth_batter; Third[3:0] = third_hitter;
  //   Third_man[3:0] = third_batter

  // Notes on the sheet:
  //   AWAY
  //   The away team bats first. 
  //   The game runs for a total of six innings. 
  //   Continue in this fashion until the sides change.
  //   The stats for batters 1–9 are stored in the ROM of the Batting_order circuit.
  //   Every time you set the Enable button to 1, the result of that plate appearance will be produced.  
  //   When the inning switches, the home team should then use the Enable button to continue.
  //   <GUIDE>
  //   TOTAL
  //   Please set up the batting order for both the home team and the away team by entering the numbers 1 through 9 without repeats.
  //   HOME
endmodule

module Batting_Order (
  input  enable_signal,
  input  [3:0] first_hitter,
  input  [3:0] second_hitter,
  input  [3:0] third_hitter,
  input  [3:0] fourth_hitter,
  input  [3:0] fifth_hitter,
  input  [3:0] sixth_hitter,
  input  [3:0] seventh_hitter,
  input  [3:0] eighth_hitter,
  input  [3:0] nineth_hitter,
  output [3:0] AVERAGE,
  output [3:0] SLUGGING,
  output [3:0] current_hitter
);

  wire [3:0] modulo_counter_1_bat_order, multiplexer_1_out, subtractor_1_out;

  modulo_counter modulo_counter_1 (.SGNL(enable_signal), .BAT_ORDER(modulo_counter_1_bat_order));
  Subtractor #(.width(4)) subtractor_1 (
    .a(modulo_counter_1_bat_order), .b(4'b0001), .out(subtractor_1_out));  // open: bin, bout
  Multiplexer #(.select(4), .width(4)) multiplexer_1 (
    .in0(first_hitter), .in1(second_hitter), .in2(third_hitter), .in3(fourth_hitter), .in4(fifth_hitter),
    .in5(sixth_hitter), .in6(seventh_hitter), .in7(eighth_hitter), .in8(nineth_hitter),
    .out(multiplexer_1_out), .sel(subtractor_1_out));  // open: in9, in10, in11, in12, in13, in14, in15
  ROM #(.addrWidth(4)) hitting (.addr(multiplexer_1_out), .data({SLUGGING, AVERAGE}));
  Adder #(.width(4)) adder_1 (.a(subtractor_1_out), .b(4'b0001), .out(current_hitter));  // open: cin, cout

  // Notes on the sheet:
  //   contents of hitting (hex, n*v repeats v):
  //   0 88 77 65 86 76 75 66 64 54
endmodule

module Base (
  input  HIT_Signal,
  input  [3:0] Average_output,
  input  [3:0] Slugging_output,
  output [3:0] total_base_output
);

  wire and_1_out, CLK, comparator_1_eq, comparator_1_gt, comparator_2_eq, comparator_2_gt, d_ff_1_qn,
       fail_to_ebh_out, fail_to_hit_out, not_1_out, not_2_out, not_3_out, not_4_out, not_5_out, not_6_out,
       not_7_out;
  wire [3:0] adder_1_out, adder_2_out, divider_1_rem, multiplexer_1_out, multiplexer_2_out,
       multiplexer_3_out, multiplexer_4_out, random_1_out, random_2_out, success_to_ebh_out;

  D_Flip_Flop d_ff_1 (.D(HIT_Signal), .clk(CLK), .Qn(d_ff_1_qn));  // open: Q, preset, reset
  Random #(.width(4)) random_1 (.clr(not_1_out), .next(d_ff_1_qn), .clk(CLK), .out(random_1_out));
  not not_1 (not_1_out, d_ff_1_qn);
  Comparator #(.mode("unsigned"), .width(4)) comparator_1 (
    .a(random_1_out), .b(Average_output), .gt(comparator_1_gt), .eq(comparator_1_eq));  // open: lt
  or fail_to_hit (fail_to_hit_out, comparator_1_gt, comparator_1_eq);
  Random #(.width(4)) random_2 (.clr(not_2_out), .next(fail_to_hit_out), .clk(CLK), .out(random_2_out));
  not not_2 (not_2_out, fail_to_hit_out);
  Clock clock_1 (.out(CLK));
  not not_3 (not_3_out, fail_to_hit_out);
  Comparator #(.mode("unsigned"), .width(4)) comparator_2 (
    .a(random_2_out), .b(Slugging_output), .gt(comparator_2_gt), .eq(comparator_2_eq));  // open: lt
  or fail_to_ebh (fail_to_ebh_out, comparator_2_gt, comparator_2_eq);
  and and_1 (and_1_out, fail_to_ebh_out, not_3_out);
  not not_4 (not_4_out, fail_to_hit_out);
  not not_5 (not_5_out, not_3_out);
  Random #(.width(4)) success_to_ebh (.clr(not_6_out), .next(and_1_out), .clk(CLK), .out(success_to_ebh_out));
  not not_6 (not_6_out, and_1_out);
  not not_7 (not_7_out, and_1_out);
  Multiplexer #(.width(4)) multiplexer_1 (.in0(4'b0000), .in1(4'b0001), .out(multiplexer_1_out), .sel(not_5_out));
  Divider #(.width(4)) divider_1 (.a(success_to_ebh_out), .b(4'b0100), .rem(divider_1_rem));  // open: out, upper
  Multiplexer #(.width(4)) multiplexer_2 (.in0(4'b0000), .in1(4'b0001), .out(multiplexer_2_out), .sel(not_7_out));
  Adder #(.width(4)) adder_1 (.a(divider_1_rem), .b(multiplexer_2_out), .out(adder_1_out));  // open: cin, cout
  Multiplexer #(.width(4)) multiplexer_3 (.in0(4'b0000), .in1(adder_1_out), .out(multiplexer_3_out), .sel(not_4_out));
  Adder #(.width(4)) adder_2 (.a(multiplexer_1_out), .b(multiplexer_3_out), .out(adder_2_out));  // open: cin, cout
  Multiplexer #(.width(4)) multiplexer_4 (.in0(4'b0000), .in1(adder_2_out), .out(multiplexer_4_out), .sel(not_3_out));
  Divider #(.width(4)) divider_2 (.a(multiplexer_4_out), .b(4'b0101), .rem(total_base_output));  // open: out, upper
endmodule

module Runner (
  input  [3:0] before_position,
  input  [3:0] bases,
  input  Enable,
  input  Inning_change,
  output [3:0] runs,
  output [3:0] after_position
);

  wire and_1_out, clock_1_out, clock_2_out, clock_3_out, clock_4_out, clock_5_out, clock_6_out, d_ff_1_q,
       d_ff_2_q, d_ff_3_q, ensignal, not_1_out;
  wire [2:0] bit_extender_1_out, bit_extender_2_out, multiplexer_1_out, shifter_1_out, shifter_2_out,
       shifter_3_out;
  wire [3:0] adder_1_out, bit_counter_1_number_of_runners, bit_counter_2_number_of_runners,
       bit_extender_3_out, multiplexer_2_out, multiplexer_3_out, or_1_out, subtractor_1_out;

  Bit_Extender #(.in_width(4), .out_width(3)) bit_extender_1 (.in(bases), .out(bit_extender_1_out));
  D_Flip_Flop d_ff_1 (.D(Enable), .clk(clock_1_out), .Q(d_ff_1_q));  // open: Qn, preset, reset
  Clock clock_1 (.out(clock_1_out));
  Bit_Extender #(.in_width(4), .out_width(3)) bit_extender_2 (.in(before_position), .out(bit_extender_2_out));
  D_Flip_Flop d_ff_2 (.D(d_ff_1_q), .clk(clock_2_out), .Q(d_ff_2_q));  // open: Qn, preset, reset
  Clock clock_2 (.out(clock_2_out));
  D_Flip_Flop d_ff_3 (.D(d_ff_2_q), .clk(clock_3_out), .Q(d_ff_3_q));  // open: Qn, preset, reset
  Clock clock_3 (.out(clock_3_out));
  Shifter #(.width(3)) shifter_1 (.in(bit_extender_2_out), .\dist (2'b01), .out(shifter_1_out));
  Shifter #(.width(3)) shifter_2 (.in(bit_extender_2_out), .\dist (2'b10), .out(shifter_2_out));
  Shifter #(.width(3)) shifter_3 (.\dist (2'b11), .out(shifter_3_out));  // open: in
  Multiplexer #(.select(3), .width(3)) multiplexer_1 (
    .in0(bit_extender_2_out), .in1(shifter_1_out), .in2(shifter_2_out), .in3(shifter_3_out), .in4(3'b000),
    .out(multiplexer_1_out), .sel(bit_extender_1_out));  // open: in5, in6, in7
  and and_1 (and_1_out, d_ff_2_q, not_1_out);
  not not_1 (not_1_out, d_ff_3_q);
  D_Flip_Flop d_ff_4 (.D(and_1_out), .clk(clock_4_out), .Q(ensignal));  // open: Qn, preset, reset
  Clock clock_4 (.out(clock_4_out));
  assign bit_extender_3_out = {{1{1'b0}}, multiplexer_1_out};  // Bit_Extender bit_extender_3
  Multiplexer #(.select(3), .width(4)) multiplexer_2 (
    .in0(4'b0000), .in1(4'b0001), .in2(4'b0010), .in3(4'b0100), .in4(4'b0000), .out(multiplexer_2_out),
    .sel(bit_extender_1_out));  // open: in5, in6, in7
  assign or_1_out = bit_extender_3_out | multiplexer_2_out;  // OR_Gate or_1, 4 bits wide
  bit_counter bit_counter_1 (
    .Position_of_runners(before_position), .number_of_runners(bit_counter_1_number_of_runners));
  bit_counter bit_counter_2 (
    .Position_of_runners(bit_extender_3_out), .number_of_runners(bit_counter_2_number_of_runners));
  Subtractor #(.width(4)) subtractor_1 (
    .a(bit_counter_1_number_of_runners), .b(bit_counter_2_number_of_runners), .out(subtractor_1_out));  // open: bin, bout
  Adder #(.width(4)) adder_1 (.a(subtractor_1_out), .b(4'b0001), .out(adder_1_out));  // open: cin, cout
  Multiplexer #(.width(4)) multiplexer_3 (
    .in0(subtractor_1_out), .in1(adder_1_out), .out(multiplexer_3_out), .sel(bit_extender_1_out[2]));
  Register #(.width(4)) register_1 (
    .D(multiplexer_3_out), .en(ensignal), .clk(clock_5_out), .Q(runs), .clr(Inning_change));
  Clock clock_5 (.out(clock_5_out));
  Register #(.width(4)) register_2 (
    .D(or_1_out), .en(ensignal), .clk(clock_6_out), .Q(after_position), .clr(Inning_change));
  Clock clock_6 (.out(clock_6_out));
endmodule

module bit_counter (
  input  [3:0] Position_of_runners,
  output [3:0] number_of_runners
);

  wire xnor_1_out, xnor_2_out, xnor_3_out, xnor_4_out;
  wire [3:0] adder_1_out, adder_2_out, adder_3_out, adder_4_out, adder_5_out, adder_6_out,
       bit_extender_1_out, bit_extender_2_out, bit_extender_3_out, bit_extender_4_out;

  xnor xnor_1 (xnor_1_out, 1'b0, Position_of_runners[0]);
  xnor xnor_2 (xnor_2_out, Position_of_runners[1], 1'b0);
  xnor xnor_3 (xnor_3_out, Position_of_runners[2], 1'b0);
  xnor xnor_4 (xnor_4_out, Position_of_runners[3], 1'b0);
  assign bit_extender_1_out = {{3{xnor_1_out}}, xnor_1_out};  // Bit_Extender bit_extender_1
  assign bit_extender_2_out = {{3{xnor_2_out}}, xnor_2_out};  // Bit_Extender bit_extender_2
  assign bit_extender_3_out = {{3{xnor_3_out}}, xnor_3_out};  // Bit_Extender bit_extender_3
  assign bit_extender_4_out = {{3{xnor_4_out}}, xnor_4_out};  // Bit_Extender bit_extender_4
  Adder #(.width(4)) adder_1 (.a(4'b0001), .b(bit_extender_1_out), .out(adder_1_out));  // open: cin, cout
  Adder #(.width(4)) adder_2 (.a(bit_extender_2_out), .b(4'b0001), .out(adder_2_out));  // open: cin, cout
  Adder #(.width(4)) adder_3 (.a(4'b0001), .b(bit_extender_3_out), .out(adder_3_out));  // open: cin, cout
  Adder #(.width(4)) adder_4 (.a(bit_extender_4_out), .b(4'b0001), .out(adder_4_out));  // open: cin, cout
  Adder #(.width(4)) adder_5 (.a(adder_1_out), .b(adder_2_out), .out(adder_5_out));  // open: cin, cout
  Adder #(.width(4)) adder_6 (.a(adder_3_out), .b(adder_4_out), .out(adder_6_out));  // open: cin, cout
  Adder #(.width(4)) adder_7 (.a(adder_5_out), .b(adder_6_out), .out(number_of_runners));  // open: cin, cout
endmodule

module Out_Counts (
  input  [3:0] total_base_input,
  input  Enable,
  output [3:0] Innings,
  output ThreeOut_signal,
  output [1:0] OUT_cnts
);

  wire and_1_out, and_2_out, and_4_out, clock_1_out, clock_2_out, clock_3_out, clock_4_out, clock_5_out,
       clock_6_out, comparator_1_eq, comparator_1_gt, d_ff_1_q, d_ff_2_q, d_ff_3_q, d_ff_4_q, d_ff_5_qn,
       j_k_ff_1_qn, j_k_ff_2_qn, j_k_ff_3_qn, multiplexer_1_out, not_1_out, or_1_out;
  wire [1:0] adder_1_out, and_3_out, bit_extender_1_out, divider_1_rem, multiplexer_2_out;
  wire [3:0] j_k_ff_1_q;

  Multiplexer #(.select(4)) multiplexer_1 (
    .in0(1'b1), .in1(1'b0), .in2(1'b0), .in3(1'b0), .in4(1'b0), .in5(1'b0), .in6(1'b0), .in7(1'b0),
    .in8(1'b0), .in9(1'b0), .in10(1'b0), .in11(1'b0), .in12(1'b0), .in13(1'b0), .in14(1'b0), .in15(1'b0),
    .out(multiplexer_1_out), .sel(total_base_input));
  D_Flip_Flop d_ff_1 (.D(Enable), .clk(clock_1_out), .Q(d_ff_1_q));  // open: Qn, preset, reset
  Clock clock_1 (.out(clock_1_out));
  D_Flip_Flop d_ff_2 (.D(d_ff_1_q), .clk(clock_2_out), .Q(d_ff_2_q));  // open: Qn, preset, reset
  Clock clock_2 (.out(clock_2_out));
  D_Flip_Flop d_ff_3 (.D(d_ff_2_q), .clk(clock_3_out), .Q(d_ff_3_q));  // open: Qn, preset, reset
  Clock clock_3 (.out(clock_3_out));
  and and_1 (and_1_out, d_ff_2_q, not_1_out);
  not not_1 (not_1_out, d_ff_3_q);
  D_Flip_Flop d_ff_4 (.D(and_1_out), .clk(clock_4_out), .Q(d_ff_4_q));  // open: Qn, preset, reset
  Clock clock_4 (.out(clock_4_out));
  Multiplexer #(.width(2)) multiplexer_2 (.in0(2'b00), .in1(2'b11), .out(multiplexer_2_out), .sel(and_2_out));
  assign bit_extender_1_out = {{1{and_2_out}}, and_2_out};  // Bit_Extender bit_extender_1
  and and_2 (and_2_out, multiplexer_1_out, d_ff_4_q);
  assign and_3_out = multiplexer_2_out & bit_extender_1_out;  // AND_Gate and_3, 2 bits wide
  D_Flip_Flop d_ff_5 (.D(and_2_out), .clk(clock_5_out), .Qn(d_ff_5_qn));  // open: Q, preset, reset
  Clock clock_5 (.out(clock_5_out));
  Divider #(.width(2)) divider_1 (.a(and_3_out), .b(2'b10), .rem(divider_1_rem));  // open: out, upper
  Adder #(.width(2)) adder_1 (.a(divider_1_rem), .b(OUT_cnts), .out(adder_1_out));  // open: cin, cout
  Register #(.width(2)) register_1 (.D(adder_1_out), .en(d_ff_5_qn), .clk(clock_6_out), .Q(OUT_cnts), .clr(or_1_out));
  Clock clock_6 (.out(clock_6_out));
  J_K_Flip_Flop j_k_ff_1 (
    .J(ThreeOut_signal), .K(ThreeOut_signal), .clk(ThreeOut_signal), .Q(j_k_ff_1_q[0]), .Qn(j_k_ff_1_qn),
    .reset(and_4_out));  // open: preset
  J_K_Flip_Flop j_k_ff_2 (
    .J(ThreeOut_signal), .K(ThreeOut_signal), .clk(j_k_ff_1_qn), .Q(j_k_ff_1_q[1]), .Qn(j_k_ff_2_qn),
    .reset(and_4_out));  // open: preset
  Multiplexer multiplexer_3 (.in0(1'b0), .in1(1'b1), .out(ThreeOut_signal), .sel(or_1_out));
  Comparator #(.mode("unsigned"), .width(2)) comparator_1 (
    .a(OUT_cnts), .b(2'b11), .gt(comparator_1_gt), .eq(comparator_1_eq));  // open: lt
  J_K_Flip_Flop j_k_ff_3 (
    .J(ThreeOut_signal), .K(ThreeOut_signal), .clk(j_k_ff_2_qn), .Q(j_k_ff_1_q[2]), .Qn(j_k_ff_3_qn),
    .reset(and_4_out));  // open: preset
  or or_1 (or_1_out, comparator_1_gt, comparator_1_eq);
  J_K_Flip_Flop j_k_ff_4 (
    .J(ThreeOut_signal), .K(ThreeOut_signal), .clk(j_k_ff_3_qn), .Q(j_k_ff_1_q[3]), .reset(and_4_out));  // open: Qn, preset
  and and_4 (and_4_out, j_k_ff_1_q[2], j_k_ff_1_q[1]);
  Adder #(.width(4)) adder_2 (.a(j_k_ff_1_q), .b(4'b0001), .out(Innings));  // open: cin, cout
endmodule

module ordering (
  input  Enable,
  input  [3:0] first,
  input  [3:0] second,
  input  [3:0] third,
  input  [3:0] fourth,
  input  [3:0] fifth,
  input  [3:0] sixth,
  input  [3:0] seventh,
  input  [3:0] eighth,
  input  [3:0] nineth,
  output [3:0] Run,
  output [3:0] POSITION,
  output [3:0] HITS_OR_OUT,
  output [1:0] OUTS,
  output [3:0] current_player,
  output [3:0] Innings
);

  wire and_1_out, clock_1_out, clock_2_out, clock_3_out, clock_4_out, clock_5_out, d_ff_1_q, d_ff_2_q,
       d_ff_3_q, ensignal, H, not_1_out, or_1_out, out_counts_1_threeout_signal;
  wire [1:0] out_counts_1_out_cnts;
  wire [3:0] base_1_total_base_output, batting_order_1_average, batting_order_1_slugging;

  D_Flip_Flop d_ff_1 (.D(Enable), .clk(clock_1_out), .Q(d_ff_1_q));  // open: Qn, preset, reset
  Clock clock_1 (.out(clock_1_out));
  Clock clock_2 (.out(clock_2_out));
  Batting_Order batting_order_1 (
    .enable_signal(Enable), .first_hitter(first), .second_hitter(second), .third_hitter(third),
    .fourth_hitter(fourth), .fifth_hitter(fifth), .sixth_hitter(sixth), .seventh_hitter(seventh),
    .eighth_hitter(eighth), .nineth_hitter(nineth), .AVERAGE(batting_order_1_average),
    .SLUGGING(batting_order_1_slugging), .current_hitter(current_player));
  D_Flip_Flop d_ff_2 (.D(d_ff_1_q), .clk(clock_2_out), .Q(d_ff_2_q));  // open: Qn, preset, reset
  D_Flip_Flop d_ff_3 (.D(d_ff_2_q), .clk(clock_3_out), .Q(d_ff_3_q));  // open: Qn, preset, reset
  Clock clock_3 (.out(clock_3_out));
  Base base_1 (
    .HIT_Signal(Enable), .Average_output(batting_order_1_average),
    .Slugging_output(batting_order_1_slugging), .total_base_output(base_1_total_base_output));
  not not_1 (not_1_out, d_ff_3_q);
  Multiplexer multiplexer_1 (.in0(1'b0), .in1(1'b1), .out(H), .sel(or_1_out));
  or or_1 (or_1_out, base_1_total_base_output[3], base_1_total_base_output[2], base_1_total_base_output[1], base_1_total_base_output[0]);
  D_Flip_Flop d_ff_4 (.D(and_1_out), .clk(clock_4_out), .Q(ensignal));  // open: Qn, preset, reset
  and and_1 (and_1_out, d_ff_2_q, not_1_out);
  Clock clock_4 (.out(clock_4_out));
  Register #(.width(4)) register_1 (
    .D(base_1_total_base_output), .en(ensignal), .clk(clock_5_out), .Q(HITS_OR_OUT));  // open: clr
  Clock clock_5 (.out(clock_5_out));
  Runner runner_1 (
    .before_position(POSITION), .bases(base_1_total_base_output), .Enable(Enable),
    .Inning_change(out_counts_1_threeout_signal), .runs(Run), .after_position(POSITION));
  Out_Counts out_counts_1 (
    .total_base_input(base_1_total_base_output), .Enable(Enable), .Innings(Innings),
    .ThreeOut_signal(out_counts_1_threeout_signal), .OUT_cnts(out_counts_1_out_cnts));
  Multiplexer #(.select(2), .width(2)) multiplexer_2 (
    .in0(2'b00), .in1(2'b01), .in2(2'b11), .in3(2'b00), .out(OUTS), .sel(out_counts_1_out_cnts));

  // Other names for the same wires on the sheet: hits[3:0] = HITS_OR_OUT; pos[3:0] = POSITION; running[3:0] = Run
endmodule

module modulo_counter (
  input  SGNL,
  output [3:0] BAT_ORDER
);

  wire and_1_out, j_k_ff_1_qn, j_k_ff_2_qn, j_k_ff_3_qn;
  wire [3:0] j_k_ff_1_q;

  J_K_Flip_Flop j_k_ff_1 (
    .J(SGNL), .K(SGNL), .clk(SGNL), .Q(j_k_ff_1_q[0]), .Qn(j_k_ff_1_qn), .reset(and_1_out));  // open: preset
  J_K_Flip_Flop j_k_ff_2 (
    .J(SGNL), .K(SGNL), .clk(j_k_ff_1_qn), .Q(j_k_ff_1_q[1]), .Qn(j_k_ff_2_qn), .reset(and_1_out));  // open: preset
  J_K_Flip_Flop j_k_ff_3 (
    .J(SGNL), .K(SGNL), .clk(j_k_ff_2_qn), .Q(j_k_ff_1_q[2]), .Qn(j_k_ff_3_qn), .reset(and_1_out));  // open: preset
  J_K_Flip_Flop j_k_ff_4 (
    .J(SGNL), .K(SGNL), .clk(j_k_ff_3_qn), .Q(j_k_ff_1_q[3]), .reset(and_1_out));  // open: Qn, preset
  and and_1 (and_1_out, j_k_ff_1_q[0], j_k_ff_1_q[3]);
  Adder #(.width(4)) adder_1 (.a(j_k_ff_1_q), .b(4'b0001), .out(BAT_ORDER));  // open: cin, cout
endmodule

module scoring (
  input  [3:0] runs,
  input  en,
  output [7:0] score
);

  wire and_1_out, clock_1_out, clock_2_out, clock_3_out, clock_4_out, clock_5_out, d_ff_1_q, d_ff_2_q,
       d_ff_3_q, ensignal, not_1_out;
  wire [7:0] bit_extender_1_out, register_1_q;

  assign bit_extender_1_out = {{4{1'b0}}, runs};  // Bit_Extender bit_extender_1
  Adder adder_1 (.a(register_1_q), .b(bit_extender_1_out), .out(score));  // open: cin, cout
  D_Flip_Flop d_ff_1 (.D(en), .clk(clock_1_out), .Q(d_ff_1_q));  // open: Qn, preset, reset
  Clock clock_1 (.out(clock_1_out));
  D_Flip_Flop d_ff_2 (.D(d_ff_1_q), .clk(clock_2_out), .Q(d_ff_2_q));  // open: Qn, preset, reset
  Clock clock_2 (.out(clock_2_out));
  Register register_1 (.D(score), .en(ensignal), .clk(clock_3_out), .Q(register_1_q));  // open: clr
  Clock clock_3 (.out(clock_3_out));
  D_Flip_Flop d_ff_3 (.D(d_ff_2_q), .clk(clock_4_out), .Q(d_ff_3_q));  // open: Qn, preset, reset
  Clock clock_4 (.out(clock_4_out));
  and and_1 (and_1_out, d_ff_2_q, not_1_out);
  not not_1 (not_1_out, d_ff_3_q);
  D_Flip_Flop d_ff_4 (.D(and_1_out), .clk(clock_5_out), .Q(ensignal));  // open: Qn, preset, reset
  Clock clock_5 (.out(clock_5_out));
endmodule

module BASEBALL (
  input  [3:0] first,
  input  [3:0] second,
  input  [3:0] third,
  input  [3:0] fourth,
  input  [3:0] fifth,
  input  [3:0] sixth,
  input  [3:0] seventh,
  input  [3:0] eighth,
  input  [3:0] nineth,
  input  in_10,
  output [4:0] H_signal,
  output [3:0] total_awayL,
  output [3:0] total_awayH,
  output [3:0] runner_position,
  output [1:0] outs,
  output [3:0] the_current,
  output [3:0] inning
);

  wire [2:0] bit_extender_1_out;
  wire [3:0] ordering_1_hits_or_out, ordering_1_run;

  ordering ordering_1 (
    .Enable(in_10), .first(first), .second(second), .third(third), .fourth(fourth), .fifth(fifth),
    .sixth(sixth), .seventh(seventh), .eighth(eighth), .nineth(nineth), .Run(ordering_1_run),
    .POSITION(runner_position), .HITS_OR_OUT(ordering_1_hits_or_out), .OUTS(outs),
    .current_player(the_current), .Innings(inning));
  Multiplexer #(.select(3), .width(5)) multiplexer_1 (
    .in0(5'b10000), .in1(5'b00001), .in2(5'b00010), .in3(5'b00100), .in4(5'b01000), .out(H_signal),
    .sel(bit_extender_1_out));  // open: in5, in6, in7
  Bit_Extender #(.in_width(4), .out_width(3), .\type ("zero")) bit_extender_1 (
    .in(ordering_1_hits_or_out), .out(bit_extender_1_out));
  scoring scoring_1 (.runs(ordering_1_run), .en(in_10), .score({total_awayH, total_awayL}));

  // Other names for the same wires on the sheet: En_signal = in_10
endmodule
